# Fritzing sketch ESP12S_auto (saved by Fritzing 0.9.3b)
breadboards: 1

parts:
  부품1 = FTDI Basic Programmer
  U1 = ESP8266 WiFi Module [part_number=ESP8266]
  C1 = Electrolytic Capacitor [capacitance=100μF package="0807 [SMD, electrolytic]"]
  R2 = Resistor [tolerance=±5% resistance=100k package="2010 [SMD]"]
  R4 = Resistor [tolerance=±5% resistance=100k package="2010 [SMD]"]
  YwRobot_Power_Supply1 = YwRobot Breadboard Power Supply [part_number=545043]
  R5 = Resistor [tolerance=±5% resistance=100k package="2010 [SMD]"]
  R6 = Resistor [tolerance=±5% resistance=100k package="2010 [SMD]"]

nets:
  N1: 부품1.DTR, U1.GPIO_0, R6.Pin_0
  N2: 부품1.RXI, U1.TXD
  N3: 부품1.TXO, U1.RXD
  GND: 부품1.GND, U1.GND, YwRobot_Power_Supply1.GND#12
  N4: U1.VCC, C1.+, R4.Pin_0, YwRobot_Power_Supply1.VCC#10, R5.Pin_0
  N5: U1.CH_PD, R4.Pin_1
  N6: U1.GPIO_15, R2.Pin_1
  N7: U1.REST, R5.Pin_1
  N8: C1.-, R2.Pin_0, YwRobot_Power_Supply1.GND#14
  N9: YwRobot_Power_Supply1.VCC#6, R6.Pin_1

custom parts:
  YwRobot Breadboard Power Supply: The YwRobot Breadboard Power Supply (MB-V2) has two power rails; they can be 5V or 3V3. Power to the module can be provided through the female USB socket or through the A10 (female) 2.1mm power jack.
