# Fritzing sketch driving robot (saved by Fritzing 0.9.3b)

parts:
  U1 = ESP8266 WiFi Module [part_number=ESP8266]
  hc-sr1 = hc-sr04
  부품1 = Arduino Uno (Rev3)
  S1 = Toggle Switch [package=THT]
  S2 = Toggle Switch [package=THT]
  IC1 = H-Bridge [package=THT]
  IC2 = H-Bridge [package=THT]
  VCC1 = Battery
  L1 = Inductor [package="400 mil [THT]"]
  L2 = Inductor [package="400 mil [THT]"]
  L3 = Inductor [package="400 mil [THT]"]
  L4 = Inductor [package="400 mil [THT]"]
  R2 = Resistor [tolerance=±5% resistance=220 package=THT]
  R3 = Resistor [tolerance=±5% resistance=220 package=THT]

nets:
  N1: U1.RXD, S2.COM
  N2: U1.VCC, U1.GPIO_0
  N3: U1.CH_PD, 부품1.3V3
  GND: U1.GND, 부품1.GND, IC2.GND3, R2.Pin_1
  N4: U1.TXD, S1.COM
  N5: U1.GPIO_15, R2.Pin_0
  N6: U1.REST, R3.Pin_1
  N7: hc-sr1.Trig, 부품1.D13/SCK
  N8: hc-sr1.Echo, 부품1.D12/MISO
  N9: 부품1.D9_PWM, IC1.1_2EN
  N10: 부품1.D0/RX, S2.L2
  N11: 부품1.D1/TX, S1.L2
  N12: 부품1.D2, IC1.2A
  N13: 부품1.D3_PWM, IC1.1A
  N14: 부품1.D4, IC2.2A
  N15: 부품1.D5_PWM, IC2.1A
  N16: 부품1.D6_PWM, S2.L1
  N17: 부품1.D7, S1.L1
  N18: IC1.1Y, L1.pin_1
  N19: IC1.2Y, L1.pin_0
  N20: IC1.3Y, L2.pin_1
  N21: IC1.4Y, L2.pin_0
  N22: IC1.VCC1, IC2.VCC1
  N23: IC2.1Y, L3.pin_1
  N24: IC2.2Y, L3.pin_0
  N25: IC2.VCC2, VCC1.+
  N26: IC2.3Y, L4.pin_1
  N27: IC2.4Y, L4.pin_0

notes:
  ESP8266(ESP-12E)
  3.3V
  HC-SR04
  DC Geared Motor x 4
